// Logisim project Proje.circ as structural Verilog
module Register (
  input  enable,
  input  clk,
  input  [19:0] \input ,
  output [19:0] \output 
);

  DFF dff_1 (.D(\input [0]), .clk(clk), .in_3(enable), .out_4(\output [0]));
  DFF dff_2 (.D(\input [1]), .clk(clk), .in_3(enable), .out_4(\output [1]));
  DFF dff_3 (.D(\input [2]), .clk(clk), .in_3(enable), .out_4(\output [2]));
  DFF dff_4 (.D(\input [3]), .clk(clk), .in_3(enable), .out_4(\output [3]));
  DFF dff_5 (.D(\input [4]), .clk(clk), .in_3(enable), .out_4(\output [4]));
  DFF dff_6 (.D(\input [5]), .clk(clk), .in_3(enable), .out_4(\output [5]));
  DFF dff_7 (.D(\input [6]), .clk(clk), .in_3(enable), .out_4(\output [6]));
  DFF dff_8 (.D(\input [7]), .clk(clk), .in_3(enable), .out_4(\output [7]));
  DFF dff_9 (.D(\input [8]), .clk(clk), .in_3(enable), .out_4(\output [8]));
  DFF dff_10 (.D(\input [9]), .clk(clk), .in_3(enable), .out_4(\output [9]));
  DFF dff_11 (.D(\input [10]), .clk(clk), .in_3(enable), .out_4(\output [10]));
  DFF dff_12 (.D(\input [11]), .clk(clk), .in_3(enable), .out_4(\output [11]));
  DFF dff_13 (.D(\input [12]), .clk(clk), .in_3(enable), .out_4(\output [12]));
  DFF dff_14 (.D(\input [13]), .clk(clk), .in_3(enable), .out_4(\output [13]));
  DFF dff_15 (.D(\input [14]), .clk(clk), .in_3(enable), .out_4(\output [14]));
  DFF dff_16 (.D(\input [15]), .clk(clk), .in_3(enable), .out_4(\output [15]));
  DFF dff_17 (.D(\input [16]), .clk(clk), .in_3(enable), .out_4(\output [16]));
  DFF dff_18 (.D(\input [17]), .clk(clk), .in_3(enable), .out_4(\output [17]));
  DFF dff_19 (.D(\input [18]), .clk(clk), .in_3(enable), .out_4(\output [18]));
  DFF dff_20 (.D(\input [19]), .clk(clk), .in_3(enable), .out_4(\output [19]));
endmodule

module DFF (
  input  D,
  input  clk,
  input  in_3,
  output out_4
);

  wire and_1_out, and_2_out, nor_1_out, not_1_out;

  not not_1 (not_1_out, D);
  and and_1 (and_1_out, D, clk, in_3);
  and and_2 (and_2_out, in_3, clk, not_1_out);
  nor nor_1 (nor_1_out, and_1_out, out_4);
  nor nor_2 (out_4, nor_1_out, and_2_out);
endmodule
